// Logisim project Jedan circ file.circ as structural Verilog: 1 circuit, main circuit main
module main (
  input  in_1,
  output out_2
);

  // AND_Gate and_1 is placed but not wired
  // OR_Gate or_1 is placed but not wired
  // NOT_Gate not_1 is placed but not wired
endmodule
